// Logisim project calculadore-adv.circ as structural Verilog: 6 circuits, main circuit soma
module main (
  input  subt,
  input  soma,
  input  in_3,
  input  in_4,
  input  in_5,
  input  in_6,
  input  in_7
);

  wire and_1_out, and_2_out, and_3_out, and_4_out, and_5_out, and_6_out, and_7_out, and_8_out, and_9_out,
       and_10_out, and_11_out, and_12_out, and_13_out, and_14_out, and_15_out, display_entrada_1_s1,
       display_entrada_1_s2, display_entrada_1_s3, display_entrada_1_s4, display_entrada_1_s5,
       display_entrada_1_s6, display_entrada_1_s7, display_entrada_2_s1, display_entrada_2_s2,
       display_entrada_2_s3, display_entrada_2_s4, display_entrada_2_s5, display_entrada_2_s6,
       display_entrada_2_s7, display_saida_1_s1, display_saida_1_s2, display_saida_1_s3, display_saida_1_s4,
       display_saida_1_s5, display_saida_1_s6, display_saida_1_s7, multiplicacao_1_s1, multiplicacao_1_s2,
       multiplicacao_1_s3, multiplicacao_1_s4, or_1_out, or_2_out, or_3_out, or_4_out, soma_1_s1, soma_1_s2,
       soma_1_s3, soma_1_s4, subtracao_1_s0, subtracao_1_s1, subtracao_1_s2, subtracao_1_s3, subtracao_1_s4;

  display_entrada display_entrada_1 (
    .A1(in_4), .A2(in_5), .S2(display_entrada_1_s2), .S1(display_entrada_1_s1), .S6(display_entrada_1_s6),
    .S7(display_entrada_1_s7), .S4(display_entrada_1_s4), .S5(display_entrada_1_s5), .S3(display_entrada_1_s3));
  _7_Segment_Display u_7_segment_display_1 (
    .g(display_entrada_1_s7), .f(display_entrada_1_s6), .a(display_entrada_1_s1), .b(display_entrada_1_s2),
    .e(display_entrada_1_s4), .d(display_entrada_1_s5), .c(display_entrada_1_s3));  // open: dp
  display_entrada display_entrada_2 (
    .A1(in_6), .A2(in_7), .S2(display_entrada_2_s2), .S1(display_entrada_2_s1), .S6(display_entrada_2_s6),
    .S7(display_entrada_2_s7), .S4(display_entrada_2_s4), .S5(display_entrada_2_s5), .S3(display_entrada_2_s3));
  _7_Segment_Display u_7_segment_display_2 (
    .g(display_entrada_2_s7), .f(display_entrada_2_s6), .a(display_entrada_2_s1), .b(display_entrada_2_s2),
    .e(display_entrada_2_s4), .d(display_entrada_2_s5), .c(display_entrada_2_s3));  // open: dp
  and and_1 (and_1_out, soma, ~subt, ~in_3);  // AND_Gate
  and and_2 (and_2_out, in_5, and_1_out);
  and and_3 (and_3_out, in_4, and_1_out);
  and and_4 (and_4_out, in_7, and_1_out);
  soma soma_1 (
    .A2(and_5_out), .S1(soma_1_s1), .A1(and_4_out), .B2(and_3_out), .S2(soma_1_s2), .B1(and_2_out),
    .S3(soma_1_s3), .S4(soma_1_s4));
  and and_5 (and_5_out, in_6, and_1_out);
  LED led_1 (.in(subtracao_1_s0));
  or or_1 (or_1_out, soma_1_s3, subtracao_1_s3, multiplicacao_1_s3);
  or or_2 (or_2_out, soma_1_s4, subtracao_1_s4, multiplicacao_1_s4);
  _7_Segment_Display u_7_segment_display_3 (
    .g(display_saida_1_s7), .f(display_saida_1_s6), .a(display_saida_1_s1), .b(display_saida_1_s2),
    .e(display_saida_1_s4), .d(display_saida_1_s5), .c(display_saida_1_s3));  // open: dp
  or or_3 (or_3_out, soma_1_s1, subtracao_1_s1, multiplicacao_1_s1);
  or or_4 (or_4_out, soma_1_s2, subtracao_1_s2, multiplicacao_1_s2);
  display_saida display_saida_1 (
    .A1(or_3_out), .A2(or_4_out), .B1(or_1_out), .B2(or_2_out), .S2(display_saida_1_s2),
    .S1(display_saida_1_s1), .S6(display_saida_1_s6), .S7(display_saida_1_s7), .S4(display_saida_1_s4),
    .S5(display_saida_1_s5), .S3(display_saida_1_s3));
  and and_6 (and_6_out, ~soma, ~subt, in_3);  // AND_Gate
  and and_7 (and_7_out, in_5, and_6_out);
  and and_8 (and_8_out, in_7, and_6_out);
  and and_9 (and_9_out, in_4, and_6_out);
  multiplicacao multiplicacao_1 (
    .A2(and_10_out), .A1(and_8_out), .B2(and_9_out), .B1(and_7_out), .S1(multiplicacao_1_s1),
    .S2(multiplicacao_1_s2), .S3(multiplicacao_1_s3), .S4(multiplicacao_1_s4));
  and and_10 (and_10_out, in_6, and_6_out);
  and and_11 (and_11_out, ~soma, subt, ~in_3);  // AND_Gate
  and and_12 (and_12_out, in_5, and_11_out);
  and and_13 (and_13_out, in_4, and_11_out);
  subtracao subtracao_1 (
    .A1(and_14_out), .A2(and_15_out), .B1(and_13_out), .B2(and_12_out), .S0(subtracao_1_s0),
    .S1(subtracao_1_s1), .S2(subtracao_1_s2), .S3(subtracao_1_s3), .S4(subtracao_1_s4));
  and and_14 (and_14_out, in_6, and_11_out);
  and and_15 (and_15_out, in_7, and_11_out);

  // Notes on the sheet:
  //   mult
  //   on = negativo
  //   off = positivo
endmodule

module soma (
  input  A2,
  input  A1,
  input  B2,
  input  B1,
  output S1,
  output S2,
  output S3,
  output S4
);

  wire and_1_out, and_2_out, and_3_out, and_4_out, and_5_out, and_6_out, and_7_out, and_8_out, and_9_out,
       and_10_out, and_11_out, not_1_out, not_2_out, not_3_out, not_4_out, not_5_out, not_6_out, not_7_out,
       not_8_out, not_9_out, not_10_out, not_11_out, not_12_out;

  and and_1 (and_1_out, A1, B2, B1);
  and and_2 (and_2_out, A2, B2);
  and and_3 (and_3_out, A2, A1, B1);
  not not_1 (not_1_out, A2);
  not not_2 (not_2_out, A1);
  not not_3 (not_3_out, A2);
  not not_4 (not_4_out, B1);
  not not_5 (not_5_out, A2);
  not not_6 (not_6_out, B2);
  not not_7 (not_7_out, A1);
  not not_8 (not_8_out, B2);
  not not_9 (not_9_out, B2);
  not not_10 (not_10_out, B1);
  not not_11 (not_11_out, A1);
  and and_4 (and_4_out, not_11_out, B1);
  and and_5 (and_5_out, A1, not_12_out);
  not not_12 (not_12_out, B1);
  or or_1 (S2, and_1_out, and_2_out, and_3_out);
  and and_6 (and_6_out, not_1_out, not_2_out, B2);
  and and_7 (and_7_out, not_3_out, B2, not_4_out);
  and and_8 (and_8_out, not_5_out, A1, not_6_out, B1);
  and and_9 (and_9_out, A2, not_7_out, not_8_out);
  and and_10 (and_10_out, A2, not_9_out, not_10_out);
  and and_11 (and_11_out, A2, A1, B2, B1);
  or or_2 (S4, and_4_out, and_5_out);
  or or_3 (S3, and_6_out, and_7_out, and_8_out, and_9_out, and_10_out, and_11_out);

  assign S1 = 1'b0;
endmodule

module multiplicacao (
  input  A2,
  input  A1,
  input  B2,
  input  B1,
  output S1,
  output S2,
  output S3,
  output S4
);

  wire and_2_out, and_3_out, and_4_out, and_5_out, and_6_out, and_7_out, not_1_out, not_2_out, not_3_out,
       not_4_out, not_5_out, not_6_out;

  and and_1 (S1, A2, A1, B2, B1);
  and and_2 (and_2_out, A2, not_1_out, B2);
  not not_1 (not_1_out, A1);
  and and_3 (and_3_out, A2, B2, not_2_out);
  not not_2 (not_2_out, B1);
  not not_3 (not_3_out, A2);
  and and_4 (and_4_out, not_3_out, A1, B2);
  and and_5 (and_5_out, A1, B2, not_4_out);
  not not_4 (not_4_out, B1);
  not not_5 (not_5_out, A1);
  and and_6 (and_6_out, A2, not_5_out, B1);
  and and_7 (and_7_out, A2, not_6_out, B1);
  not not_6 (not_6_out, B2);
  and and_8 (S4, A1, B1);
  or or_1 (S2, and_2_out, and_3_out);
  or or_2 (S3, and_4_out, and_5_out, and_6_out, and_7_out);
endmodule

module display_entrada (
  input  A1,
  input  A2,
  output S2,
  output S1,
  output S6,
  output S7,
  output S4,
  output S5,
  output S3
);

  wire not_1_out, not_2_out, not_3_out, not_4_out, not_6_out;

  not not_1 (not_1_out, A2);
  not not_2 (not_2_out, A1);
  not not_3 (not_3_out, A2);
  not not_4 (not_4_out, A2);
  not not_5 (S5, A2);
  not not_6 (not_6_out, A1);
  or or_1 (S1, not_1_out, A1);
  and and_1 (S6, not_2_out, not_3_out);
  or or_2 (S4, not_4_out, A1);
  or or_3 (S3, not_6_out, A2);

  assign S2 = 1'b1;
  assign S7 = A1;
endmodule

module display_saida (
  input  A1,
  input  A2,
  input  B1,
  input  B2,
  output S2,
  output S1,
  output S6,
  output S7,
  output S4,
  output S5,
  output S3
);

  wire and_1_out, and_2_out, and_3_out, and_4_out, and_5_out, and_6_out, and_7_out, and_8_out, and_9_out,
       and_10_out, and_11_out, and_12_out, and_13_out, and_14_out, and_15_out, and_16_out, and_17_out,
       and_18_out, and_19_out, and_20_out, and_21_out, and_22_out, and_23_out, and_24_out, and_25_out,
       and_26_out, and_27_out, and_28_out, and_29_out, and_30_out, and_31_out, and_32_out, and_33_out,
       and_34_out, and_35_out, and_36_out, not_1_out, not_2_out, not_3_out, not_4_out, not_5_out, not_6_out,
       not_7_out, not_8_out, not_9_out, not_10_out, not_11_out, not_12_out, not_13_out, not_14_out,
       not_15_out, not_16_out, not_17_out, not_18_out, not_19_out, not_20_out, not_21_out, not_22_out,
       not_23_out, not_24_out, not_25_out, not_26_out, not_27_out, not_28_out, not_29_out, not_30_out,
       not_31_out, not_32_out, not_33_out, not_34_out, not_35_out, not_36_out, not_37_out, not_38_out,
       not_39_out, not_40_out, not_41_out, not_42_out, not_43_out;

  not not_1 (not_1_out, A1);
  and and_1 (and_1_out, not_1_out, not_2_out);
  not not_2 (not_2_out, A2);
  not not_3 (not_3_out, A1);
  and and_2 (and_2_out, not_3_out, not_4_out, not_5_out);
  not not_4 (not_4_out, B1);
  not not_5 (not_5_out, B2);
  not not_6 (not_6_out, A2);
  and and_3 (and_3_out, not_6_out, not_7_out);
  not not_7 (not_7_out, B1);
  not not_8 (not_8_out, A2);
  and and_4 (and_4_out, not_8_out, not_9_out);
  not not_9 (not_9_out, B2);
  not not_10 (not_10_out, A1);
  and and_5 (and_5_out, not_10_out, B1, B2);
  not not_11 (not_11_out, B1);
  and and_6 (and_6_out, A1, not_11_out, B2);
  not not_12 (not_12_out, A2);
  and and_7 (and_7_out, not_12_out, not_13_out);
  not not_13 (not_13_out, B2);
  not not_14 (not_14_out, A1);
  and and_8 (and_8_out, not_14_out, B1);
  not not_15 (not_15_out, A1);
  and and_9 (and_9_out, not_15_out, A2, B2);
  and and_10 (and_10_out, A2, B1);
  and and_11 (and_11_out, A1, not_16_out, not_17_out);
  not not_16 (not_16_out, A2);
  not not_17 (not_17_out, B1);
  and and_12 (and_12_out, A1, not_18_out);
  not not_18 (not_18_out, B2);
  not not_19 (not_19_out, B1);
  and and_13 (and_13_out, not_19_out, not_20_out);
  not not_20 (not_20_out, B2);
  not not_21 (not_21_out, A1);
  and and_14 (and_14_out, not_21_out, A2, not_22_out);
  not not_22 (not_22_out, B1);
  and and_15 (and_15_out, A2, not_23_out);
  not not_23 (not_23_out, B2);
  and and_16 (and_16_out, A1, not_24_out);
  not not_24 (not_24_out, A2);
  and and_17 (and_17_out, A1, B1);
  not not_25 (not_25_out, A2);
  and and_18 (and_18_out, not_25_out, B1);
  and and_19 (and_19_out, B1, not_26_out);
  not not_26 (not_26_out, B2);
  not not_27 (not_27_out, A1);
  and and_20 (and_20_out, not_27_out, A2, not_28_out);
  not not_28 (not_28_out, B1);
  and and_21 (and_21_out, A1, not_29_out);
  not not_29 (not_29_out, A2);
  and and_22 (and_22_out, A1, B2);
  not not_30 (not_30_out, A2);
  and and_23 (and_23_out, not_30_out, not_31_out);
  not not_31 (not_31_out, B2);
  not not_32 (not_32_out, A2);
  and and_24 (and_24_out, not_32_out, B1);
  and and_25 (and_25_out, B1, not_33_out);
  not not_33 (not_33_out, B2);
  not not_34 (not_34_out, B1);
  and and_26 (and_26_out, A2, not_34_out, B2);
  and and_27 (and_27_out, A1, A2);
  not not_35 (not_35_out, A2);
  and and_28 (and_28_out, not_35_out, not_36_out);
  not not_36 (not_36_out, B2);
  and and_29 (and_29_out, B1, not_37_out);
  not not_37 (not_37_out, B2);
  and and_30 (and_30_out, A1, B1);
  and and_31 (and_31_out, A1, A2);
  not not_38 (not_38_out, A1);
  and and_32 (and_32_out, not_38_out, not_39_out);
  not not_39 (not_39_out, B1);
  not not_40 (not_40_out, A1);
  and and_33 (and_33_out, not_40_out, B2);
  not not_41 (not_41_out, B1);
  and and_34 (and_34_out, not_41_out, B2);
  not not_42 (not_42_out, A1);
  and and_35 (and_35_out, not_42_out, A2);
  and and_36 (and_36_out, A1, not_43_out);
  not not_43 (not_43_out, A2);
  or or_1 (S6, and_13_out, and_14_out, and_15_out, and_16_out, and_17_out);
  or or_2 (S7, and_18_out, and_19_out, and_20_out, and_21_out, and_22_out);
  or or_3 (S4, and_23_out, and_24_out, and_25_out, and_26_out, and_27_out);
  or or_4 (S5, and_28_out, and_29_out, and_30_out, and_31_out);
  or or_5 (S3, and_32_out, and_33_out, and_34_out, and_35_out, and_36_out);
  or or_6 (S2, and_1_out, and_2_out, and_3_out, and_4_out, and_5_out, and_6_out);
  or or_7 (S1, and_7_out, and_8_out, and_9_out, and_10_out, and_11_out, and_12_out);
endmodule

module subtracao (
  input  A1,
  input  A2,
  input  B1,
  input  B2,
  output S0,
  output S1,
  output S2,
  output S3,
  output S4
);

  wire and_1_out, and_2_out, and_3_out, and_4_out, and_5_out, and_6_out, and_7_out, and_8_out, and_9_out,
       not_1_out, not_2_out, not_3_out, not_4_out, not_5_out, not_6_out, not_7_out, not_8_out, not_9_out,
       not_10_out, not_11_out, not_12_out;

  not not_1 (not_1_out, A1);
  not not_2 (not_2_out, A2);
  and and_1 (and_1_out, not_1_out, not_2_out, B2);
  not not_3 (not_3_out, A1);
  and and_2 (and_2_out, not_3_out, B1);
  not not_4 (not_4_out, A2);
  and and_3 (and_3_out, not_4_out, B1, B2);
  not not_5 (not_5_out, A1);
  and and_4 (and_4_out, not_5_out, not_6_out, B1);
  not not_6 (not_6_out, A2);
  not not_7 (not_7_out, A1);
  and and_5 (and_5_out, not_7_out, B1, B2);
  and and_6 (and_6_out, A1, not_8_out, not_9_out);
  not not_8 (not_8_out, B1);
  not not_9 (not_9_out, B2);
  and and_7 (and_7_out, A1, A2, not_10_out);
  not not_10 (not_10_out, B1);
  not not_11 (not_11_out, A2);
  and and_8 (and_8_out, not_11_out, B2);
  and and_9 (and_9_out, A2, not_12_out);
  not not_12 (not_12_out, B2);
  or or_1 (S0, and_1_out, and_2_out, and_3_out);
  or or_2 (S3, and_4_out, and_5_out, and_6_out, and_7_out);
  or or_3 (S4, and_8_out, and_9_out);

  assign S1 = 1'b0;
  assign S2 = 1'b0;
endmodule
