// Logisim project ram-4x1.circ as structural Verilog: 1 circuit, main circuit main
module main (
  input  in_1,
  input  in_2,
  input  in_3,
  input  in_4
);

  wire and_1_out, and_2_out, and_3_out, and_4_out, and_5_out, and_6_out, and_7_out, and_8_out, and_9_out,
       and_10_out, and_11_out, and_12_out, and_13_out, and_14_out, and_15_out, and_16_out, not_1_out,
       or_1_out, s_r_ff_1_q, s_r_ff_2_q, s_r_ff_3_q, s_r_ff_4_q;

  not not_1 (not_1_out, in_3);
  and and_1 (and_1_out, ~in_1, ~in_2);  // AND_Gate
  and and_2 (and_2_out, in_3, and_1_out);
  and and_3 (and_3_out, not_1_out, and_1_out);
  and and_4 (and_4_out, and_1_out, s_r_ff_1_q);
  S_R_Flip_Flop s_r_ff_1 (.S(and_2_out), .clk(in_4), .R(and_3_out), .Q(s_r_ff_1_q));  // open: Qn, preset, reset, en
  and and_5 (and_5_out, ~in_1, in_2);  // AND_Gate
  and and_6 (and_6_out, in_3, and_5_out);
  and and_7 (and_7_out, not_1_out, and_5_out);
  S_R_Flip_Flop s_r_ff_2 (.S(and_6_out), .clk(in_4), .R(and_7_out), .Q(s_r_ff_2_q));  // open: Qn, preset, reset, en
  and and_8 (and_8_out, and_5_out, s_r_ff_2_q);
  and and_9 (and_9_out, in_1, ~in_2);  // AND_Gate
  and and_10 (and_10_out, in_3, and_9_out);
  and and_11 (and_11_out, not_1_out, and_9_out);
  S_R_Flip_Flop s_r_ff_3 (.S(and_10_out), .clk(in_4), .R(and_11_out), .Q(s_r_ff_3_q));  // open: Qn, preset, reset, en
  and and_12 (and_12_out, and_9_out, s_r_ff_3_q);
  and and_13 (and_13_out, in_1, in_2);
  and and_14 (and_14_out, in_3, and_13_out);
  S_R_Flip_Flop s_r_ff_4 (.S(and_14_out), .clk(in_4), .R(and_15_out), .Q(s_r_ff_4_q));  // open: Qn, preset, reset, en
  and and_15 (and_15_out, not_1_out, and_13_out);
  and and_16 (and_16_out, and_13_out, s_r_ff_4_q);
  or or_1 (or_1_out, and_16_out, and_12_out, and_8_out, and_4_out);
endmodule
